# Fritzing sketch ADIRU (saved by Fritzing 0.9.4)
breadboards: 1

parts:
  R2 = Resistor [tolerance=±5% resistance=4.7k package=THT]
  IR2 = RM-series Subminiature Rotary Switch
  R3 = Resistor [tolerance=±5% resistance=100 package=THT]
  C1 = Capacitor [package=0805]
  IR3 = RM-series Subminiature Rotary Switch
  R4 = Resistor [tolerance=±5% resistance=100 package=THT]
  IR1 = RM-series Subminiature Rotary Switch
  R5 = Resistor [tolerance=±5% resistance=100 package=THT]
  C3 = Capacitor [package=0805]
  R6 = Resistor [tolerance=±5% resistance=4.7k package=THT]
  Part1 = Arduino Mega 2560 (Rev3)
  C2 = Capacitor [package=0805]

nets:
  GND: R2.Pin_0, IR2.1, C1.2, IR3.1, IR1.1, C3.2, Part1.GND, C2.2
  2.5V: R2.Pin_1, IR2.2, IR3.2, IR1.2, R6.Pin_1
  N1: IR2.0, R3.Pin_1, C1.1
  5V: IR2.3, IR3.3, IR1.3, R6.Pin_0, Part1.5V
  A4: R3.Pin_0, Part1.A4
  N2: IR3.0, R4.Pin_1, C2.1
  A3: R4.Pin_0, Part1.A3
  N3: IR1.0, R5.Pin_1, C3.1
  A2: R5.Pin_0, Part1.A2

notes:
  Airbus A320 Home Cockpit, ADIRU - IRx Rotary Switches, 1.0
