# Fritzing sketch ADIRS (saved by Fritzing 0.9.4)
circuit board: 12.6cm x 3.79999cm
breadboards: 2

parts:
  HCMS-2912/3 = HCMS-29xx
  HCMS-2912/2 = HCMS-29xx
  HCMS-2912/1 = HCMS-29xx
  R1 = Resistor [tolerance=±5% resistance=100 package=THT]
  R7 = Resistor [tolerance=±5% resistance=100 package=THT]
  C2 = Ceramic Capacitor [capacitance=2.2µF package="100 mil [THT, multilayer]"]
  C1 = Ceramic Capacitor [capacitance=2.2µF package="100 mil [THT, multilayer]"]
  R9 = Resistor [tolerance=±5% resistance=3.3k package=THT]
  R10 = Resistor [tolerance=±5% resistance=3.3k package=THT]
  R8 = Resistor [tolerance=±5% resistance=3.3k package=THT]
  R6 = Resistor [tolerance=±5% resistance=2.2k package=THT]
  R5 = Resistor [tolerance=±5% resistance=2.2k package=THT]
  R2 = Resistor [tolerance=±5% resistance=2.2k package=THT]
  R3 = Resistor [tolerance=±5% resistance=2.2k package=THT]
  R4 = Resistor [tolerance=±5% resistance=2.2k package=THT]
  J2 = double row male pin header, 14 pins [form="♂ (male)"]
  J1 = double row male pin header, 10 pins [form="♂ (male)"]

nets:
  5V/rotary 0-5/rotary 1-3: HCMS-2912/3.V_LED, HCMS-2912/3.VLED, HCMS-2912/3.SEL, HCMS-2912/3.V_Logic, HCMS-2912/2.V_LED, HCMS-2912/2.VLED, HCMS-2912/2.SEL, HCMS-2912/2.V_Logic, HCMS-2912/1.V_LED, HCMS-2912/1.VLED, HCMS-2912/1.SEL, HCMS-2912/1.V_Logic, R10.Pin_0, R6.Pin_0, J2.pin3, J2.pin12, J1.pin5
  GND/rotary 0-0/rotary 1-0: HCMS-2912/3.Gnd_LED, HCMS-2912/3.Blank, HCMS-2912/3.GND_Logic, HCMS-2912/2.Gnd_LED, HCMS-2912/2.Blank, HCMS-2912/2.GND_Logic, HCMS-2912/1.Gnd_LED, HCMS-2912/1.Blank, HCMS-2912/1.GND_Logic, C2.0, C1.0, R8.Pin_1, R2.Pin_1, J2.pin4, J2.pin11, J1.pin4
  N1: HCMS-2912/3.Data_In, HCMS-2912/2.Data_Out
  RS: HCMS-2912/3.RS, HCMS-2912/2.RS, HCMS-2912/1.RS, J1.pin7
  CLOCK: HCMS-2912/3.Clock, HCMS-2912/2.Clock, HCMS-2912/1.Clock, J1.pin8
  CE: HCMS-2912/3.Chip_Enable, HCMS-2912/2.Chip_Enable, HCMS-2912/1.Chip_Enable, J1.pin9
  RESET: HCMS-2912/3.Reset, HCMS-2912/2.Reset, HCMS-2912/1.Reset, J1.pin10
  N2: HCMS-2912/2.Data_In, HCMS-2912/1.Data_Out
  DATA IN: HCMS-2912/1.Data_In, J1.pin6
  A0: R1.Pin_0, J1.pin1
  N3: R1.Pin_1, C1.1, J2.pin2
  A1: R7.Pin_0, J1.pin2
  N4: R7.Pin_1, C2.1, J2.pin5
  rotary 1-2: R9.Pin_0, R10.Pin_1, J2.pin14
  rotary 1-1: R9.Pin_1, R8.Pin_0, J2.pin1
  rotary 0-4: R6.Pin_1, R5.Pin_0, J2.pin6
  rotary 0-3: R5.Pin_1, R4.Pin_0, J2.pin7
  rotary 0-1: R2.Pin_0, R3.Pin_1, J2.pin9
  rotary 0-2: R3.Pin_0, R4.Pin_1, J2.pin8

notes:
  Airbus A320 Home Cockpit, ADIRS 2020.06, 3.0
  Adrian Buenter
  ADIRS 2020.06
  1
  8
  6
  to spoke of rotary-0
  to spoke of rotary-1
  1-1
  0-sp
  0-5
  0-0
  1-sp
  0-4
  0-3
  0-2
  0-1
  1-0
  1-3
  1-2
  A0
  A1
  GND
  NC
  +5V
  DATAIN
  RS
  CLOCK
  CE
  RESET
  Rotary wiring:
  0-0: DATA TEST
  0-1: DATA TK/GS
  0-2: DATA PPOS
  0-3: DATA WIND
  0-4: DATA HEADING
  0-5: STS
  1-0: SYS OFF
  1-1: SYS IR1
  1-2: SYS IR3
  1-3: SYS IR2
