# Fritzing sketch BAT (saved by Fritzing 0.9.4)
circuit board: 16.24cm x 6.50001cm
breadboards: 1

parts:
  J4_BAT1_(7-12) = female pin header, 6 pins [form="♀ (female)"]
  J3_BAT1_(1-6) = female pin header, 6 pins [form="♀ (female)"]
  J2_BAT2_(7-12) = female pin header, 6 pins [form="♀ (female)"]
  J1_BAT2_(1-6) = female pin header, 6 pins [form="♀ (female)"]
  U1_MAX7219 = MAX7219 [part_number=MAX7219 package=dil24]
  R1 = Resistor [tolerance=±5% resistance=10k package=THT]
  J5 = male pin header, 5 pins [form="♂ (male)"]
  J6 = male pin header, 5 pins [form="♂ (male)"]
  C1 = Ceramic Capacitor [capacitance=0.1µF package="100 mil [THT, multilayer]"]

nets:
  SEGB: J4_BAT1_(7-12).pin1, J2_BAT2_(7-12).pin1, U1_MAX7219.SEGB
  DIG5: J4_BAT1_(7-12).pin2, U1_MAX7219.DIG5
  DIG6: J4_BAT1_(7-12).pin3, U1_MAX7219.DIG6
  SEGF: J4_BAT1_(7-12).pin4, J2_BAT2_(7-12).pin4, U1_MAX7219.SEGF
  SEGA: J4_BAT1_(7-12).pin5, J2_BAT2_(7-12).pin5, U1_MAX7219.SEGA
  DIG7: J4_BAT1_(7-12).pin6, U1_MAX7219.DIG7
  SEGE: J3_BAT1_(1-6).pin1, J1_BAT2_(1-6).pin1, U1_MAX7219.SEGE
  SEGD: J3_BAT1_(1-6).pin2, J1_BAT2_(1-6).pin2, U1_MAX7219.SEGD
  SEGDP: J3_BAT1_(1-6).pin3, J1_BAT2_(1-6).pin3, U1_MAX7219.SEGDP
  SEGC: J3_BAT1_(1-6).pin4, J1_BAT2_(1-6).pin4, U1_MAX7219.SEGC
  SEGG: J3_BAT1_(1-6).pin5, J1_BAT2_(1-6).pin5, U1_MAX7219.SEGG
  DIG4: J3_BAT1_(1-6).pin6, U1_MAX7219.DIG4
  DIG1: J2_BAT2_(7-12).pin2, U1_MAX7219.DIG1
  DIG2: J2_BAT2_(7-12).pin3, U1_MAX7219.DIG2
  DIG3: J2_BAT2_(7-12).pin6, U1_MAX7219.DIG3
  DIG0: J1_BAT2_(1-6).pin6, U1_MAX7219.DIG0
  DIN: U1_MAX7219.DIN, J5.pin3
  GND/GND2: U1_MAX7219.GND, U1_MAX7219.GND2, J5.pin2, J6.pin2, C1.1
  LOAD: U1_MAX7219.LOAD, J5.pin4, J6.pin4
  CLK: U1_MAX7219.CLK, J5.pin5, J6.pin5
  N1: U1_MAX7219.ISET, R1.Pin_0
  VCC: U1_MAX7219.VCC, R1.Pin_1, J5.pin1, J6.pin1, C1.0
  DOUT: U1_MAX7219.DOUT, J6.pin3

notes:
  Airbus A320 Home Cockpit, Battery Display BAT1/2 2020.06, 1.0
  BAT1
  BAT2
  BATTERY 2020.06
  Adrian Buenter
  VCC
  GND
  DIN
  DOUT
  LOAD
  CLK
  1
  7
